# Fritzing sketch bike (saved by Fritzing 0.9.4)
breadboards: 6

parts:
  GY521_-_MPU6050_-_Accelerometer = InvenSense MPU6050
  LED_Blue = smd LED [color="Blue (430nm)" package="1206 [SMD]"]
  KY003_-_Hall_Sensor = KY-003 Hall Magnetic Sensor Module [package="Breakout board"]
  LED_Red = smd LED [color="Red (633nm)" package="1206 [SMD]"]
  R_330 = Resistor [tolerance=±5% resistance=330 package="1206 [SMD]"]
  R_330_2 = Resistor [tolerance=±5% resistance=330 package="1206 [SMD]"]
  Button_+ = Pushbutton [package="[SMD]"]
  Button_L = Pushbutton [package="[SMD]"]
  Button_R = Pushbutton [package="[SMD]"]
  Button_B = Pushbutton [package="[SMD]"]
  Button_A = Pushbutton [package="[SMD]"]
  R_10K = Resistor [tolerance=±5% resistance=10k package=THT]
  R_10K_2 = Resistor [tolerance=±5% resistance=10k package=THT]
  R_10K1 = Resistor [tolerance=±5% resistance=10k package=THT]
  R_10K_3 = Resistor [tolerance=±5% resistance=10k package=THT]
  R_10K_4 = Resistor [tolerance=±5% resistance=10k package=THT]
  Arduino_Leonardo = Arduino Leonardo (Rev3b)
  SPDT_LeftJS_Interruptor = SWITCH_SPDT [package=kps-1290]  # not connected
  LED_Green = smd LED [color="Green (555nm)" package="0805 [SMD]"]
  R_330_3 = Resistor [tolerance=±5% resistance=330 package="1206 [SMD]"]
  Manual_Left_Joystick = Thumb Joystick  # not connected

nets:
  VCC: GY521_-_MPU6050_-_Accelerometer.VCC, R_10K.Pin_1, R_10K_2.Pin_1, R_10K1.Pin_1, R_10K_3.Pin_1, R_10K_4.Pin_1, Arduino_Leonardo.5V
  GND: GY521_-_MPU6050_-_Accelerometer.GND, LED_Blue.cathode, KY003_-_Hall_Sensor.-, LED_Red.cathode, Button_+.Pin_3, Button_+.Pin_4, Button_L.Pin_3, Button_L.Pin_4, Button_R.Pin_3, Button_R.Pin_4, Button_B.Pin_3, Button_B.Pin_4, Button_A.Pin_3, Button_A.Pin_4, Arduino_Leonardo.GND, LED_Green.cathode
  N1: GY521_-_MPU6050_-_Accelerometer.SCL, Arduino_Leonardo.D3_PWM/SCL
  N2: GY521_-_MPU6050_-_Accelerometer.SDA, Arduino_Leonardo.D2/SDA
  N3: GY521_-_MPU6050_-_Accelerometer.INT, Arduino_Leonardo.D0/RX
  N4: LED_Blue.anode, R_330.Pin_0
  N5: KY003_-_Hall_Sensor.S, Arduino_Leonardo.D8/A8
  VIN: KY003_-_Hall_Sensor.Vin, Arduino_Leonardo.3V3
  N6: LED_Red.anode, R_330_2.Pin_0
  N7: R_330.Pin_1, Arduino_Leonardo.D12/A11
  N8: R_330_2.Pin_1, Arduino_Leonardo.D13_PWM
  N9: Button_+.Pin_1, Button_+.Pin_2, R_10K_4.Pin_0, Arduino_Leonardo.D5_PWM
  N10: Button_L.Pin_1, Button_L.Pin_2, R_10K_2.Pin_0, Arduino_Leonardo.D7
  N11: Button_R.Pin_1, Button_R.Pin_2, R_10K.Pin_0, Arduino_Leonardo.D6_PWM/A7
  N12: Button_B.Pin_1, Button_B.Pin_2, R_10K_3.Pin_0, Arduino_Leonardo.D1/TX
  N13: Button_A.Pin_1, Button_A.Pin_2, R_10K1.Pin_0, Arduino_Leonardo.D4/A6
  N14: Arduino_Leonardo.D9_PWM/A9, R_330_3.Pin_1
  N15: LED_Green.anode, R_330_3.Pin_0

custom parts:
  KY-003 Hall Magnetic Sensor Module: KEYES KY-003 Arduino Hall Magnetic Sensor Module is a switch that will turn on/off in the presence of a magnetic field.
